// Logisim project ALU.circ as structural Verilog: 1 circuit, main circuit ALU
module ALU (
  input  [31:0] A,
  input  [31:0] B,
  input  [4:0] Shift,
  input  [3:0] Codop,
  input  CarryIn,
  output [31:0] S,
  output [3:0] Flags
);

  wire bitselector_3_out, bitselector_4_out, bitselector_6_out, bitselector_8_out, CInBarre, comparator_1_eq,
       comparator_2_eq, comparator_3_eq, comparator_4_eq, leftshiftL, leftshiftR;
  wire [4:0] subtractor_3_out, subtractor_4_out;
  wire [31:0] AandB, AfoisB, AorB, AplusB, AplusBplusCIn, ASR, AxorB, BandNotA, BmoinsA, BmoinsAplusCInBarre,
       LSL, LSR, not_1_out, not_2_out, notA, rotR, zero, ZeromoinsA;

  assign AandB = A & B;  // AND_Gate AandB, 32 bits wide
  assign AxorB = A ^ B;  // XOR_Gate AxorB, 32 bits wide
  Adder #(.width(32)) adder_1 (.a(A), .b(B), .out(AplusB));  // open: cin, cout
  Subtractor #(.width(32)) subtractor_1 (.a(B), .b(A), .out(BmoinsA));  // open: bin, bout
  Adder #(.width(32)) adder_2 (.a(A), .b(B), .out(AplusBplusCIn), .cin(CarryIn));  // open: cout
  Adder #(.width(32)) adder_3 (.a(BmoinsA), .out(BmoinsAplusCInBarre), .cin(CInBarre));  // open: b, cout
  Negator #(.width(1)) negator_1 (.in(CarryIn), .out(CInBarre));
  Subtractor #(.width(32)) subtractor_2 (.a({32{1'b0}}), .b(A), .out(ZeromoinsA));  // open: bin, bout
  Multiplier #(.width(32)) multiplier_1 (.a(A), .b(B), .out(AfoisB));  // open: cin, cout
  assign not_1_out = ~A;  // NOT_Gate not_1, 32 bits wide
  assign zero = A & not_1_out;  // AND_Gate ZERO, 32 bits wide
  assign not_2_out = ~A;  // NOT_Gate not_2, 32 bits wide
  assign BandNotA = not_2_out & B;  // AND_Gate BandNotA, 32 bits wide
  assign notA = ~A;  // NOT_Gate not_3, 32 bits wide
  assign AorB = A | B;  // OR_Gate AorB, 32 bits wide
  Multiplexer #(.select(4), .width(32)) multiplexer_1 (
    .in0(AandB), .in1(AxorB), .in2(LSL), .in3(LSR), .in4(ASR), .in5(AplusBplusCIn),
    .in6(BmoinsAplusCInBarre), .in7(rotR), .in8(AandB), .in9(ZeromoinsA), .in10(BmoinsA), .in11(AplusB),
    .in12(AorB), .in13(AfoisB), .in14(BandNotA), .in15(notA), .out(S), .sel(Codop));
  Shifter #(.width(32)) shifter_1 (.in(B), .\dist (Shift), .out(LSL));
  Shifter #(.shift("lr"), .width(32)) shifter_2 (.in(B), .\dist (Shift), .out(LSR));
  Shifter #(.shift("ar"), .width(32)) shifter_3 (.in(B), .\dist (Shift), .out(ASR));
  Shifter #(.shift("rr"), .width(32)) shifter_4 (.in(B), .\dist (Shift), .out(rotR));
  Subtractor #(.width(5)) subtractor_3 (.a({5{1'b0}}), .b(Shift), .out(subtractor_3_out));  // open: bin, bout
  Subtractor #(.width(5)) subtractor_4 (.a(Shift), .b(5'b00001), .out(subtractor_4_out));  // open: bin, bout
  BitSelector #(.width(32)) bitselector_1 (.in(B), .out(leftshiftL), .sel(subtractor_3_out));
  BitSelector #(.width(32)) bitselector_2 (.in(B), .out(leftshiftR), .sel(subtractor_4_out));
  BitSelector #(.width(32)) bitselector_3 (.in(S), .out(bitselector_3_out), .sel({5{1'b1}}));
  BitSelector #(.width(32)) bitselector_4 (.in(AandB), .out(bitselector_4_out), .sel({5{1'b1}}));
  BitSelector #(.width(32)) bitselector_5 (.in(AandB), .out(bitselector_4_out), .sel({5{1'b1}}));
  BitSelector #(.width(32)) bitselector_6 (.in(BmoinsA), .out(bitselector_6_out), .sel({5{1'b1}}));
  BitSelector #(.width(32)) bitselector_7 (.in(BmoinsA), .out(bitselector_6_out), .sel({5{1'b1}}));
  BitSelector #(.width(32)) bitselector_8 (.in(AplusB), .out(bitselector_8_out), .sel({5{1'b1}}));
  Multiplexer #(.select(2)) multiplexer_2 (
    .in0(bitselector_3_out), .in1(bitselector_4_out), .in2(bitselector_6_out), .in3(bitselector_8_out),
    .out(Flags[3]));  // open: sel
  Multiplexer #(.select(4)) multiplexer_3 (
    .in0(1'b0), .in1(1'b0), .in2(leftshiftL), .in3(leftshiftR), .in4(leftshiftR));  // open: in5, in6, in7, in8, in9, in10, in11, in12, in13, in14, in15, out, sel
  Comparator #(.width(32)) comparator_1 (.a(S), .b({32{1'b0}}), .eq(comparator_1_eq));  // open: gt, lt
  Comparator #(.width(32)) comparator_2 (.a(AandB), .b({32{1'b0}}), .eq(comparator_2_eq));  // open: gt, lt
  Comparator #(.width(32)) comparator_3 (.a(BmoinsA), .b({32{1'b0}}), .eq(comparator_3_eq));  // open: gt, lt
  Comparator #(.width(32)) comparator_4 (.a(AplusB), .b({32{1'b0}}), .eq(comparator_4_eq));  // open: gt, lt
  Multiplexer #(.select(2)) multiplexer_4 (
    .in0(comparator_1_eq), .in1(comparator_2_eq), .in2(comparator_3_eq), .in3(comparator_4_eq), .out(Flags[2]));  // open: sel
  Multiplexer #(.select(4)) multiplexer_5 ();  // open: in0, in1, in2, in3, in4, in5, in6, in7, in8, in9, in10, in11, in12, in13, in14, in15, out, sel

  // Other names for the same wires on the sheet: CIn = CarryIn; V = Flags[0]; C = Flags[1]; Z = Flags[2];
  //   N = Flags[3]

  // Notes on the sheet:
  //   Note: for ROR, C = N
  //   Note 2: assume that shift > 0 for LSL and LSR
endmodule
