// Logisim project Ctl_Data_Processing.circ as structural Verilog: 1 circuit, main circuit Data_Processing
module Data_Processing (
  input  Enable,
  input  [15:0] Instruction,
  output [2:0] Rd,
  output [2:0] Rn,
  output [2:0] Rm,
  output [3:0] ALU_Opcode,
  output [3:0] Flags_Update_Mask
);

  wire C, V;
  wire [2:0] E3;
  wire [3:0] E4;

  Multiplexer #(.select(4)) multiplexer_1 (
    .in0(1'b0), .in1(1'b0), .in2(1'b0), .in3(1'b0), .in4(1'b0), .in5(1'b1), .in6(1'b1), .in7(1'b0),
    .in8(1'b0), .in9(1'b1), .in10(1'b1), .in11(1'b1), .in12(1'b0), .in13(1'b0), .in14(1'b0), .in15(1'b0),
    .out(V), .sel(Instruction[9:6]));
  Multiplexer #(.select(4)) multiplexer_2 (
    .in0(1'b0), .in1(1'b0), .in2(1'b1), .in3(1'b1), .in4(1'b1), .in5(1'b1), .in6(1'b1), .in7(1'b1),
    .in8(1'b0), .in9(1'b1), .in10(1'b1), .in11(1'b1), .in12(1'b0), .in13(1'b0), .in14(1'b0), .in15(1'b0),
    .out(C), .sel(Instruction[9:6]));
  assign E4 = {{3{Enable}}, Enable};  // Bit_Extender bit_extender_1
  assign E3 = {{2{Enable}}, Enable};  // Bit_Extender bit_extender_2
  assign Rd = E3 & Instruction[2:0];  // AND_Gate and_1, 3 bits wide
  assign Rn = E3 & Instruction[2:0];  // AND_Gate and_2, 3 bits wide
  assign Rm = E3 & Instruction[5:3];  // AND_Gate and_3, 3 bits wide
  assign ALU_Opcode = E4 & Instruction[9:6];  // AND_Gate and_4, 4 bits wide
  assign Flags_Update_Mask = {2'b11, C, V} & E4;  // AND_Gate and_5, 4 bits wide

  // Other names for the same wires on the sheet: E = Enable; Last3Bits[2:0] = Instruction[2:0];
  //   First3Bits[2:0] = Instruction[5:3]; ALU[3:0] = Instruction[9:6]

  // Notes on the sheet:
  //   Note 2: RSB instruction has Rn as 1st operand.
  //   MUL instruction has Rn as 1st operand and Rdm as 2nd operand
  //   For simplification purposes, Rm is used for 1st operand both here and in the ALU.
  //   Note: instructions that does not save the result will still have the second operand as the destination register, the ALU will copy the second register to the destination register
  //   Pull output low on Enable = 0
endmodule
