// Logisim project Ctl_Shift_Add_Sub_Mov.circ as structural Verilog: 1 circuit, main circuit Shift_Add_Sub_Mov
module Shift_Add_Sub_Mov (
  input  Enable,
  input  [15:0] Instruction,
  output [3:0] Flags_Update_Mask,
  output Carry,
  output Imm32_Enable,
  output [2:0] Rm,
  output [2:0] Rn,
  output [2:0] Rd,
  output [4:0] Imm5,
  output [31:0] Imm32,
  output [3:0] ALU_Opcode
);

  wire and_1_out, and_2_out, C, Ca, comparator_1_eq, comparator_1_gt, comparator_1_lt, comparator_2_lt,
       comparator_3_gt, comparator_4_lt, Imm32E, multiplexer_1_out, or_1_out, V;
  wire [2:0] E3, Imm3, RD_t, RM_t, RmOrImm3;
  wire [3:0] ALU, E4;
  wire [4:0] E5;
  wire [31:0] bit_extender_1_out, bit_extender_2_out, E32, Imm32_t;

  Comparator #(.width(3)) comparator_1 (
    .a(Instruction[13:11]), .b(3'b100), .gt(comparator_1_gt), .eq(comparator_1_eq), .lt(comparator_1_lt));
  Multiplexer multiplexer_1 (.in0(1'b0), .in1(1'b1), .out(multiplexer_1_out), .sel(comparator_2_lt));
  Comparator #(.width(3)) comparator_2 (.a(Instruction[13:11]), .b(3'b011), .lt(comparator_2_lt));  // open: gt, eq
  and and_1 (and_1_out, Instruction[9], Instruction[10], Instruction[11]);
  and and_2 (and_2_out, Instruction[10], Instruction[11], Instruction[13]);
  or or_1 (or_1_out, comparator_1_gt, comparator_1_lt);
  xor xor_1 (V, comparator_1_eq, multiplexer_1_out);
  or or_2 (Ca, and_1_out, and_2_out);
  xor xor_2 (C, comparator_1_eq, or_1_out);
  Multiplexer #(.width(3)) multiplexer_2 (
    .in0(Instruction[2:0]), .in1(Instruction[10:8]), .out(RD_t), .sel(Instruction[13]));
  Multiplexer #(.select(5), .width(4)) multiplexer_3 (
    .in0(4'b0010), .in1(4'b0010), .in2(4'b0010), .in3(4'b0010), .in4(4'b0011), .in5(4'b0011), .in6(4'b0011),
    .in7(4'b0011), .in8(4'b0100), .in9(4'b0100), .in10(4'b0100), .in11(4'b0100), .in12(4'b0101),
    .in13(4'b0110), .in14(4'b0101), .in15(4'b0110), .in16(4'b1111), .in17(4'b1111), .in18(4'b1111),
    .in19(4'b1111), .in20(4'b1100), .in21(4'b1100), .in22(4'b1100), .in23(4'b1100), .in24(4'b0101),
    .in25(4'b0101), .in26(4'b0101), .in27(4'b0101), .in28(4'b0110), .in29(4'b0110), .in30(4'b0110),
    .in31(4'b0110), .out(ALU), .sel(Instruction[13:9]));
  assign bit_extender_1_out = {{29{Imm3[2]}}, Imm3};  // Bit_Extender bit_extender_1
  assign bit_extender_2_out = {{24{Instruction[7]}}, Instruction[7:0]};  // Bit_Extender bit_extender_2
  Comparator #(.width(3)) comparator_3 (.a(Instruction[13:11]), .b(3'b100), .gt(comparator_3_gt));  // open: eq, lt
  Multiplexer #(.select(2), .width(3)) multiplexer_4 (
    .in0(Instruction[5:3]), .in1(Instruction[5:3]), .in2(Instruction[5:3]), .in3(Instruction[10:8]),
    .out(RmOrImm3), .sel(Instruction[12:11]));
  Demultiplexer #(.width(3)) demultiplexer_1 (.out0(RM_t), .out1(Imm3), .in(RmOrImm3), .sel(comparator_4_lt));
  Comparator #(.width(3)) comparator_4 (.a(Instruction[13:11]), .b(3'b011), .lt(comparator_4_lt));  // open: gt, eq
  Multiplexer #(.width(32)) multiplexer_5 (
    .in0(bit_extender_1_out), .in1(bit_extender_2_out), .out(Imm32_t), .sel(comparator_3_gt));
  assign E3 = {{2{Enable}}, Enable};  // Bit_Extender bit_extender_3
  assign E4 = {{3{Enable}}, Enable};  // Bit_Extender bit_extender_4
  assign E5 = {{4{Enable}}, Enable};  // Bit_Extender bit_extender_5
  assign E32 = {{31{Enable}}, Enable};  // Bit_Extender bit_extender_6
  Multiplexer #(.select(4)) multiplexer_6 (
    .in0(1'b0), .in1(1'b0), .in2(1'b0), .in3(1'b0), .in4(1'b0), .in5(1'b0), .in6(1'b0), .in7(1'b1),
    .in8(1'b1), .in9(1'b1), .in10(1'b1), .in11(1'b1), .in12(1'b1), .in13(1'b1), .in14(1'b1), .in15(1'b1),
    .out(Imm32E), .sel(Instruction[13:10]));
  assign Flags_Update_Mask = E4 & {2'b11, C, V};  // AND_Gate and_3, 4 bits wide
  and and_4 (Carry, Enable, Ca);
  and and_5 (Imm32_Enable, Enable, Imm32E);
  assign Rm = E3 & RM_t;  // AND_Gate and_6, 3 bits wide
  assign Rn = E3 & Instruction[5:3];  // AND_Gate and_7, 3 bits wide
  assign Rd = E3 & RD_t;  // AND_Gate and_8, 3 bits wide
  assign Imm5 = E5 & Instruction[10:6];  // AND_Gate and_9, 5 bits wide
  assign Imm32 = E32 & Imm32_t;  // AND_Gate and_10, 32 bits wide
  assign ALU_Opcode = E4 & ALU;  // AND_Gate and_11, 4 bits wide

  // Other names for the same wires on the sheet: E = Enable; Bit2_0[2:0] = Instruction[2:0];
  //   Imm8[7:0] = Instruction[7:0]; Instr[15:0] = Instruction; Bit5_3[2:0] = Instruction[5:3];
  //   RN_t[2:0] = Instruction[5:3]; Bit8_6[2:0] = Instruction[8:6]; Imm5_t[4:0] = Instruction[10:6];
  //   Bit10_8[2:0] = Instruction[10:8]; Opcode[4:0] = Instruction[13:9]; ForImm32_E[3:0] = Instruction[13:10];
  //   Bit12_11[1:0] = Instruction[12:11]; Flags[2:0] = Instruction[13:11]; Bit13 = Instruction[13]

  // Notes on the sheet:
  //   Note: ALU uses Rn register for shifts. Use Rn instead of Rm for shifts (immediate) here too
  //   Note 2: MOV uses RSB ALU opcode with Imm8 reversed so that it is copied to output register
  //   Note 3: Imm32_Enable forces the use of the immediate for Rm register
  //   Pull output low on Enable = 0
  //   only ADD and SUB use Rm
  //   Enable carry for SUB since it is reversed in ALU
  //   ALU will use Imm32 instead of Rm
endmodule
